// Logisim project COMP_303_FinalProject.circ as structural Verilog: 4 circuits, main circuit Register File
module Register_File (
  input  [15:0] WriteData,
  input  RegWrite,
  input  [3:0] ReadAddr1,
  input  [3:0] WriteAddr,
  input  in_5,
  input  [3:0] ReadAddr2,
  output [15:0] ReadData1,
  output [15:0] ReadData2
);

  wire decoder_1_out0, decoder_1_out1, decoder_1_out2, decoder_1_out3, decoder_1_out4, decoder_1_out5,
       decoder_1_out6, decoder_1_out7, decoder_1_out8, decoder_1_out9, decoder_1_out10, decoder_1_out11,
       decoder_1_out12, decoder_1_out13, decoder_1_out14, decoder_1_out15;
  wire [15:0] reg0_q, reg1_q, reg2_q, reg3_q, register_1_q, register_2_q, register_3_q, register_4_q,
       register_5_q, register_6_q, register_7_q, register_8_q, register_9_q, register_10_q, register_11_q,
       register_12_q;

  Decoder #(.select(4)) decoder_1 (
    .out0(decoder_1_out0), .out1(decoder_1_out1), .out2(decoder_1_out2), .out3(decoder_1_out3),
    .out4(decoder_1_out4), .out5(decoder_1_out5), .out6(decoder_1_out6), .out7(decoder_1_out7),
    .out8(decoder_1_out8), .out9(decoder_1_out9), .out10(decoder_1_out10), .out11(decoder_1_out11),
    .out12(decoder_1_out12), .out13(decoder_1_out13), .out14(decoder_1_out14), .out15(decoder_1_out15),
    .sel(WriteAddr), .en(RegWrite));
  Register #(.width(16)) reg0 (.D(WriteData), .en(decoder_1_out0), .Q(reg0_q), .clk(in_5));  // open: clr
  Register #(.width(16)) register_1 (.D(WriteData), .en(decoder_1_out4), .Q(register_1_q), .clk(in_5));  // open: clr
  Register #(.width(16)) register_2 (.D(WriteData), .en(decoder_1_out8), .Q(register_2_q), .clk(in_5));  // open: clr
  Register #(.width(16)) register_3 (.D(WriteData), .en(decoder_1_out12), .Q(register_3_q), .clk(in_5));  // open: clr
  Register #(.width(16)) reg1 (.D(WriteData), .en(decoder_1_out1), .Q(reg1_q), .clk(in_5));  // open: clr
  Register #(.width(16)) register_4 (.D(WriteData), .en(decoder_1_out5), .Q(register_4_q), .clk(in_5));  // open: clr
  Register #(.width(16)) register_5 (.D(WriteData), .en(decoder_1_out9), .Q(register_5_q), .clk(in_5));  // open: clr
  Register #(.width(16)) register_6 (.D(WriteData), .en(decoder_1_out13), .Q(register_6_q), .clk(in_5));  // open: clr
  Register #(.width(16)) reg2 (.D(WriteData), .en(decoder_1_out2), .Q(reg2_q), .clk(in_5));  // open: clr
  Register #(.width(16)) register_7 (.D(WriteData), .en(decoder_1_out6), .Q(register_7_q), .clk(in_5));  // open: clr
  Register #(.width(16)) register_8 (.D(WriteData), .en(decoder_1_out10), .Q(register_8_q), .clk(in_5));  // open: clr
  Register #(.width(16)) register_9 (.D(WriteData), .en(decoder_1_out14), .Q(register_9_q), .clk(in_5));  // open: clr
  Register #(.width(16)) reg3 (.D(WriteData), .en(decoder_1_out3), .Q(reg3_q), .clk(in_5));  // open: clr
  Register #(.width(16)) register_10 (.D(WriteData), .en(decoder_1_out7), .Q(register_10_q), .clk(in_5));  // open: clr
  Register #(.width(16)) register_11 (.D(WriteData), .en(decoder_1_out11), .Q(register_11_q), .clk(in_5));  // open: clr
  Register #(.width(16)) register_12 (.D(WriteData), .en(decoder_1_out15), .Q(register_12_q), .clk(in_5));  // open: clr
  Multiplexer #(.select(4), .width(16)) multiplexer_1 (
    .in0(reg0_q), .in1(reg1_q), .in2(reg2_q), .in3(reg3_q), .in4(register_1_q), .in5(register_4_q),
    .in6(register_7_q), .in7(register_10_q), .in8(register_2_q), .in9(register_5_q), .in10(register_8_q),
    .in11(register_11_q), .in12(register_3_q), .in13(register_6_q), .in14(register_9_q),
    .in15(register_12_q), .out(ReadData1), .sel(ReadAddr1));  // open: en
  Multiplexer #(.select(4), .width(16)) multiplexer_2 (
    .in0(reg0_q), .in1(reg1_q), .in2(reg2_q), .in3(reg3_q), .in4(register_1_q), .in5(register_4_q),
    .in6(register_7_q), .in7(register_10_q), .in8(register_2_q), .in9(register_5_q), .in10(register_8_q),
    .in11(register_11_q), .in12(register_3_q), .in13(register_6_q), .in14(register_9_q),
    .in15(register_12_q), .out(ReadData2), .sel(ReadAddr2));  // open: en
endmodule

module Full_Adder (
  input  A,
  input  B,
  input  C_in,
  output Sum,
  output C_out
);

  wire and_1_out, and_2_out, xor_1_out;

  xor xor_1 (xor_1_out, A, B);
  and and_1 (and_1_out, C_in, xor_1_out);
  and and_2 (and_2_out, A, B);
  xor xor_2 (Sum, xor_1_out, C_in);
  or or_1 (C_out, and_1_out, and_2_out);
endmodule

module _16_Bit_Adder (
  input  [15:0] in_1,
  input  [15:0] in_2,
  output [15:0] out_3,
  output out_4
);

  wire and_1_out, full_adder_1_c_out, full_adder_2_c_out, full_adder_3_c_out, full_adder_4_c_out,
       full_adder_5_c_out, full_adder_6_c_out, full_adder_7_c_out, full_adder_8_c_out, full_adder_9_c_out,
       full_adder_10_c_out, full_adder_11_c_out, full_adder_12_c_out, full_adder_13_c_out,
       full_adder_14_c_out;

  and and_1 (and_1_out, in_2[0], in_1[0]);
  Full_Adder full_adder_1 (
    .A(in_1[4]), .B(in_2[4]), .C_in(full_adder_12_c_out), .Sum(out_3[4]), .C_out(full_adder_1_c_out));
  Full_Adder full_adder_2 (
    .A(in_1[8]), .B(in_2[8]), .C_in(full_adder_13_c_out), .Sum(out_3[8]), .C_out(full_adder_2_c_out));
  Full_Adder full_adder_3 (
    .A(in_1[12]), .B(in_2[12]), .C_in(full_adder_14_c_out), .Sum(out_3[12]), .C_out(full_adder_3_c_out));
  xor xor_1 (out_3[0], in_1[0], in_2[0]);
  Full_Adder full_adder_4 (.A(in_1[1]), .B(in_2[1]), .C_in(and_1_out), .Sum(out_3[1]), .C_out(full_adder_4_c_out));
  Full_Adder full_adder_5 (
    .A(in_1[5]), .B(in_2[5]), .C_in(full_adder_1_c_out), .Sum(out_3[5]), .C_out(full_adder_5_c_out));
  Full_Adder full_adder_6 (
    .A(in_1[9]), .B(in_2[9]), .C_in(full_adder_2_c_out), .Sum(out_3[9]), .C_out(full_adder_6_c_out));
  Full_Adder full_adder_7 (
    .A(in_1[13]), .B(in_2[13]), .C_in(full_adder_3_c_out), .Sum(out_3[13]), .C_out(full_adder_7_c_out));
  Full_Adder full_adder_8 (
    .A(in_1[2]), .B(in_2[2]), .C_in(full_adder_4_c_out), .Sum(out_3[2]), .C_out(full_adder_8_c_out));
  Full_Adder full_adder_9 (
    .A(in_1[6]), .B(in_2[6]), .C_in(full_adder_5_c_out), .Sum(out_3[6]), .C_out(full_adder_9_c_out));
  Full_Adder full_adder_10 (
    .A(in_1[10]), .B(in_2[10]), .C_in(full_adder_6_c_out), .Sum(out_3[10]), .C_out(full_adder_10_c_out));
  Full_Adder full_adder_11 (
    .A(in_1[14]), .B(in_2[14]), .C_in(full_adder_7_c_out), .Sum(out_3[14]), .C_out(full_adder_11_c_out));
  Full_Adder full_adder_12 (
    .A(in_1[3]), .B(in_2[3]), .C_in(full_adder_8_c_out), .Sum(out_3[3]), .C_out(full_adder_12_c_out));
  Full_Adder full_adder_13 (
    .A(in_1[7]), .B(in_2[7]), .C_in(full_adder_9_c_out), .Sum(out_3[7]), .C_out(full_adder_13_c_out));
  Full_Adder full_adder_14 (
    .A(in_1[11]), .B(in_2[11]), .C_in(full_adder_10_c_out), .Sum(out_3[11]), .C_out(full_adder_14_c_out));
  Full_Adder full_adder_15 (.A(in_1[15]), .B(in_2[15]), .C_in(full_adder_11_c_out), .Sum(out_3[15]), .C_out(out_4));
endmodule

module ALU (
);

  _16_Bit_Adder u_16_bit_adder_1 ();  // open: in_1, in_2, out_3, out_4
  Subtractor #(.width(16)) subtractor_1 ();  // open: a, b, out, bin, bout
  Multiplier #(.width(16)) multiplier_1 ();  // open: a, b, out, cin, cout
  // AND_Gate and_1 is placed but not wired
  // OR_Gate or_1 is placed but not wired
  Shifter #(.width(16)) shifter_1 ();  // open: in, dist, out
  Comparator #(.width(16)) comparator_1 ();  // open: a, b, gt, eq, lt
endmodule
